// Logisim project cpu.circ as structural Verilog: 1 circuit, main circuit cpu
module cpu (
  input  clk,
  input  [31:0] Instruction,
  input  [31:0] MemReadData,
  output [31:0] MemAddress,
  output [31:0] ProgramCounter,
  output [31:0] ra,
  output [31:0] sp,
  output [31:0] t0,
  output [31:0] t1,
  output [31:0] t2,
  output [31:0] s0,
  output [31:0] s1,
  output [31:0] a0,
  output [3:0] MemWriteMask,
  output [31:0] MemWriteData
);

  wire ASel, BrEq, BrLt, BrUn, BSel, MemWEn, PCSel, RegWEn;
  wire [1:0] WBSel;
  wire [2:0] ImmSel;
  wire [3:0] ALUSel;
  wire [31:0] adder_1_out, ALUA, ALUB, DataToReg, Imm, Instruction2, multiplexer_1_out, multiplexer_2_out,
       PC4, ProgramCounter2, RegWriteData, RRD1, RRD2;

  Adder #(.width(32)) adder_1 (.a(ProgramCounter), .b(32'h4), .out(adder_1_out));  // open: cin, cout
  Multiplexer #(.width(32)) multiplexer_1 (.in0(adder_1_out), .in1(MemAddress), .out(multiplexer_1_out), .sel(PCSel));
  Multiplexer #(.width(32)) multiplexer_2 (.in0(Instruction), .in1(32'h13), .out(multiplexer_2_out), .sel(PCSel));
  Register #(.width(32)) PC (.D(multiplexer_1_out), .clk(clk), .Q(ProgramCounter));  // open: en, clr
  Register #(.width(32)) register_1 (.D(multiplexer_2_out), .clk(clk), .Q(Instruction2));  // open: en, clr
  Register #(.width(32)) register_2 (.D(ProgramCounter), .clk(clk), .Q(ProgramCounter2));  // open: en, clr
  Adder #(.width(32)) adder_2 (.a(32'h4), .b(ProgramCounter2), .out(PC4));  // open: cin, cout
  imm_gen imm_gen_1 (.Instruction(Instruction2), .ImmSel(ImmSel), .Immediate(Imm));
  control_logic control_logic_1 (
    .PCSel(PCSel), .RegWEn(RegWEn), .ImmSel(ImmSel), .BrUn(BrUn), .ASel(ASel), .BSel(BSel), .ALUSel(ALUSel),
    .MemWEn(MemWEn), .WBSel(WBSel), .Instruction(Instruction2), .BrEq(BrEq), .BrLt(BrLt));
  Multiplexer #(.width(32)) multiplexer_3 (.in0(RRD1), .in1(ProgramCounter2), .out(ALUA), .sel(ASel));
  Multiplexer #(.width(32)) multiplexer_4 (.in0(RRD2), .in1(Imm), .out(ALUB), .sel(BSel));
  regfile regfile_1 (
    .ReadReg1(Instruction2[19:15]), .ReadReg2(Instruction2[24:20]), .WriteReg(Instruction2[11:7]),
    .RegWriteData(RegWriteData), .RegWEn(RegWEn), .clk(clk), .ra(ra), .sp(sp), .t0(t0), .t1(t1), .t2(t2),
    .s0(s0), .s1(s1), .a0(a0), .RegReadData1(RRD1), .RegReadData2(RRD2));
  Multiplexer #(.select(2), .width(32)) multiplexer_5 (
    .in0(DataToReg), .in1(MemAddress), .in2(PC4), .out(RegWriteData), .sel(WBSel));  // open: in3
  branch_comp branch_comp_1 (.BrData1(RRD1), .BrData2(RRD2), .BrUn(BrUn), .BrEq(BrEq), .BrLt(BrLt));
  alu alu_1 (.ALUResult(MemAddress), .A(ALUA), .B(ALUB), .ALUSel(ALUSel));
  // imm_gen imm_gen_2: pin names not known
  partial_load partial_load_1 (
    .Instruction(Instruction2), .MemAddress(MemAddress), .DataFromMem(MemReadData), .DataToReg(DataToReg));
  partial_store partial_store_1 (
    .Instruction(Instruction2), .MemAddress(MemAddress), .DataFromReg(RRD2), .MemWEn(MemWEn),
    .MemWriteMask(MemWriteMask), .DataToMem(MemWriteData));
  // branch_comp branch_comp_2: pin names not known

  // Other names for the same wires on the sheet: ALUR[31:0] = MemAddress; rd[4:0] = Instruction2[11:7];
  //   rs1[4:0] = Instruction2[19:15]; rs2[4:0] = Instruction2[24:20]

  // Notes on the sheet:
  //   To IMEM
  //   IMEM (do **NOT** move this)
  //   From IMEM
  //   Inputs/Outputs for testing. Do **NOT** move these.
  //   It is OK to move the PC, RegFile, ALU, MEM, Branch Comp, Imm Gen, Partial Load, Partial Store and Control Logic to wherever is most convenient for you when constructing your CPU, and to delete this text
  //   To DMEM
  //   DMEM (do **NOT** move this)
  //   From DMEM
endmodule
