// Logisim project partial-store.circ as structural Verilog: 1 circuit, main circuit partial_store
module partial_store (
  input  [31:0] Instruction,
  input  [31:0] MemAddress,
  input  [31:0] DataFromReg,
  input  MemWEn,
  output [3:0] MemWriteMask,
  output [31:0] DataToMem
);

  wire [3:0] multiplexer_1_out, multiplexer_2_out, multiplexer_3_out;

  Multiplexer #(.select(2), .width(4)) multiplexer_1 (
    .in0(4'b0001), .in1(4'b0010), .in2(4'b0100), .in3(4'b1000), .out(multiplexer_1_out), .sel(MemAddress[1:0]));
  Multiplexer #(.select(2), .width(4)) multiplexer_2 (
    .in0(4'b0011), .in2(4'b1100), .out(multiplexer_2_out), .sel(MemAddress[1:0]));  // open: in1, in3
  Multiplexer #(.select(2), .width(4)) multiplexer_3 (
    .in0(multiplexer_1_out), .in1(multiplexer_2_out), .in2(4'b1111), .out(multiplexer_3_out),
    .sel(Instruction[13:12]));  // open: in3
  Multiplexer #(.width(4)) multiplexer_4 (.in0(4'b0000), .in1(multiplexer_3_out), .out(MemWriteMask), .sel(MemWEn));
  Multiplexer #(.select(2), .width(32)) multiplexer_5 (
    .in0({DataFromReg[7:0], DataFromReg[7:0], DataFromReg[7:0], DataFromReg[7:0]}),
    .in1({DataFromReg[15:0], DataFromReg[15:0]}), .in2(DataFromReg), .out(DataToMem), .sel(Instruction[13:12]));  // open: in3

  // Other names for the same wires on the sheet: MUXMem[1:0] = Instruction[13:12]; MemSel12[1:0] = MemAddress[1:0]

  // Notes on the sheet:
  //   INPUTS to your circuit
  //   DON'T CHANGE THE LOCATIONS OF THE INPUTS AND OUTPUTS!
  //   OUTPUT from your circuit
endmodule
